# Fritzing sketch Circuit imprimé final (saved by Fritzing 0.9.4)
circuit board: 9.5cm x 7cm
breadboards: 1

parts:
  LEVEE_CHARGE = Camdenboss CTB0158-2 [part_number=CTB0158-2 package=THT]
  PIN_MOTEUR_DROIT = Camdenboss CTB0158-2 [part_number=CTB0158-2 package=THT]
  PINMOTEURPWM = Camdenboss CTB0158-2 [part_number=CTB0158-2 package=THT]
  PINMOTEURGAUCHE = Camdenboss CTB0158-2 [part_number=CTB0158-2 package=THT]
  ULTRASON = Camdenboss CTB0158-2 [part_number=CTB0158-2 package=THT]
  LCD_SCREEN = Camdenboss CTB0158-4 [part_number=CTB0158-4 package=THT]
  MASSE_CAPTEURS = Camdenboss CTB0158-2 [part_number=CTB0158-2 package=THT]
  ALIM_CAPTEURS = Camdenboss CTB0158-2 [part_number=CTB0158-2 package=THT]
  LED2 = LED - 3mm [color="Red (633nm)" package="3 mm [THT]"]
  SIGNAUX_CAPTEURS = Camdenboss CTB0158-2 [part_number=CTB0158-2 package=THT]
  LED1 = LED - 3mm [color="Red (633nm)" package="3 mm [THT]"]
  Composant1 = Arduino Uno (Rev3)
  LEVEE_DE_CHARGE = Camdenboss CTB0158-2 [part_number=CTB0158-2 package=THT]
  S2 = Pushbutton [package="[THT]"]

nets:
  N1: LEVEE_CHARGE.pin1, Composant1.D1/TX
  N2: LEVEE_CHARGE.pin2, Composant1.D0/RX
  N3: PIN_MOTEUR_DROIT.pin1, Composant1.D3_PWM
  N4: PIN_MOTEUR_DROIT.pin2, Composant1.D2
  N5: PINMOTEURPWM.pin1, Composant1.D6_PWM
  N6: PINMOTEURPWM.pin2, Composant1.D5_PWM
  N7: PINMOTEURGAUCHE.pin1, Composant1.D8
  N8: PINMOTEURGAUCHE.pin2, Composant1.D7
  N9: ULTRASON.pin1, Composant1.D10_PWM/SS
  N10: ULTRASON.pin2, Composant1.D11_PWM/MOSI
  N11: LCD_SCREEN.pin1, Composant1.A3
  N12: LCD_SCREEN.pin2, Composant1.A2
  N13: LCD_SCREEN.pin3, MASSE_CAPTEURS.pin1, MASSE_CAPTEURS.pin2, LED2.cathode, LED1.cathode, Composant1.A0, Composant1.GND, S2.Pin_1, S2.Pin_2, S2.Pin_3, S2.Pin_4
  N14: LCD_SCREEN.pin4, ALIM_CAPTEURS.pin1, ALIM_CAPTEURS.pin2, Composant1.5V
  N15: LED2.anode, SIGNAUX_CAPTEURS.pin1, Composant1.D13/SCK
  N16: SIGNAUX_CAPTEURS.pin2, LED1.anode, Composant1.D12/MISO
  N17: Composant1.D9_PWM, LEVEE_DE_CHARGE.pin2
  N18: Composant1.D4, LEVEE_DE_CHARGE.pin1
